# Fritzing sketch one-digit (saved by Fritzing 0.8.5b)
breadboards: 1

parts:
  Part1 = Arduino Micro (Rev3)  # not connected
  U1 = 7-SEGMENT-DISPLAY-1_-RED [package=7-segment-1_pth]
  U2 = SUP500F [package=sup500f]  # not connected
  R1 = Resistor [tolerance=±5% resistance=10k package=THT]
  R2 = Resistor [tolerance=±5% resistance=10k package=THT]
  R3 = Resistor [tolerance=±5% resistance=10k package=THT]
  R4 = Resistor [tolerance=±5% resistance=10k package=THT]
  R5 = Resistor [tolerance=±5% resistance=10k package=THT]
  R6 = Resistor [tolerance=±5% resistance=10k package=THT]
  R7 = Resistor [tolerance=±5% resistance=10k package=THT]
  R8 = Resistor [tolerance=±5% resistance=10k package=THT]

nets:
  N1: U1.E, R1.Pin_0
  N2: U1.D, R2.Pin_0
  N3: U1.C, R3.Pin_0
  N4: U1.DP, R4.Pin_0
  N5: U1.B, R8.Pin_0
  N6: U1.A, R7.Pin_0
  N7: U1.F, R6.Pin_0
  N8: U1.G, R5.Pin_0
